# Fritzing sketch CNC_brain_box (saved by Fritzing 0.9.3b)
breadboards: 1

parts:
  J1 = ATX24 Pin Power Supply Connector [package=atx24_right_angle]
  UI_Controller = Arduino Uno (Rev3)
  U1 = RELAY [package=relay-t9a]
  Spindle = RELAY [package=relay-t9a]
  Laser = Round Pushbutton
  Tool = Round Pushbutton
  Spindle_2 = Round Pushbutton
  E-Stop = SPDT Slide Switch [package=ayz0202]
  U3 = 3.5mm Audio Jack [package=audio-jack-3.5mm-smd]  # not connected
  AC_Power = Power plug
  X1 = USB Connectors [package=usb-a-s]  # not connected
  Acc1 = SWITCH-DPDT [package=mss22]  # not connected
  Acc2 = SWITCH-DPDT [package=mss22]  # not connected
  DC_Spindle_Man_/_PWM = SWITCH-DPDT [package=mss22]  # not connected
  S1 = SPST Switch [package=switche-dpdt]
  GRBL = Rotoshield - Motor driver shield for Arduino
  AC_Tool_Relay = RELAY [package=relay-t9a]
  AC_Tool_Out = Power plug
  U4 = LCD-16X2 [package=lcd-8x2-kit]  # not connected
  U5 = WS2801 [package=sop-14]
  AC_Spindle_Man_/_Auto = SWITCH-DPDT [package=mss22]

nets:
  GND: J1.GND, UI_Controller.GND, U1.COIL2, Spindle.COIL2, Laser.leg0, Tool.leg0, Spindle_2.leg0, AC_Power.GND, AC_Tool_Out.GND
  N1: J1.PWR_OK, S1.S, AC_Tool_Relay.NO
  12V: J1.12V, UI_Controller.5V, E-Stop.2, U5.VCC
  N2: UI_Controller.D2, Laser.leg1
  N3: UI_Controller.D3_PWM, Tool.leg1
  N4: UI_Controller.D4, Spindle_2.leg1
  N5: UI_Controller.D5_PWM, Spindle.COIL1
  N6: UI_Controller.D6_PWM, U1.COIL1
  N7: U1.NC, E-Stop.1
  N8: Spindle.MAIN, GRBL.VIN
  N9: Spindle.NC, AC_Spindle_Man_/_Auto.1
  N10: AC_Power.VCC, S1.P
  N11: AC_Tool_Relay.COIL1, AC_Spindle_Man_/_Auto.2
  N12: AC_Tool_Relay.NC, AC_Tool_Out.VCC

// code stored in the sketch: brain_box.ino

